# Fritzing sketch projeto (saved by Fritzing 0.9.3b)
breadboards: 1

parts:
  Componente1 = Arduino Uno (Rev3) - ICSP [part_number="ARDUINO UNO CH340 SMD"]
  ENC28J1 = ENC28J60 [part_number=ENC28J60]  # not connected
  Mod1 = zmpt101b [part_number=ZMPT101B]
  DHT2 = DHT11 Humitidy and Temperature Sensor [part_number=DHT11]
  J1 = shrouded pin header, 10 pins [form="♂ (shrouded male)"]

nets:
  N1: Componente1.A0, DHT2.DATA
  N2: Componente1.A1, Mod1.OUT
  N3: Componente1.D10_PWM/SS, J1.pin9
  N4: Componente1.D11_PWM/MOSI, J1.pin8
  N5: Componente1.D12/MISO, J1.pin4
  N6: Componente1.D13/SCK, J1.pin3
  N7: Componente1.D2, J1.pin5
  N8: Componente1.RESET, J1.pin2
  N9: Componente1.3V3, J1.pin10
  5V: Componente1.5V, Mod1.VCC, DHT2.VDD
  GND: Componente1.GND, Mod1.GND, DHT2.GND, J1.pin1

custom parts:
  ENC28J60: Ethernet Module ENC28J60
  zmpt101b: Single phase ac active output voltate transformer module.
  DHT11 Humitidy and Temperature Sensor: DHT11 Humidity and Temperature Sensor
